# Fritzing sketch Control Led RGB Arduino Ethernet (saved by Fritzing 0.9.3b)
circuit board: 8.46667cm x 5.64444cm
breadboards: 2

parts:
  Composant1 = Arduino Mega 2560 (Rev3)
  2N2222 = NPN-Transistor [package="TO92 [THT]"]
  1K = Resistor [tolerance=±5% resistance=220 package=THT]
  L7805CV = Voltage Regulator [package=to-220-alt]
  J1 = Power Jack [package=power_jack_smd]
  IC1 = ULN2003A [package="DIP16 [THT]"]
  LED1 = RGB LED (com. anode, rbg) [package="5 mm [THT]"]
  K3 = Relay [part_number=FRS1B-S package=THT]
  Q4 = NPN-Transistor [package="TO92 [THT]"]
  D4 = Rectifier Diode [part_number=1N4001 package="300 mil [THT]"]
  R5 = Resistor [resistance=1k tolerance=±5% package=THT]
  R6 = Resistor [tolerance=±5% resistance=220 package=THT]
  LED2 = LED - 5mm [color="Red (633nm)" package="5 mm [THT]"]

nets:
  GND: Composant1.GND, 2N2222.C, L7805CV.IN, J1.GND, IC1.0V, Q4.E, LED2.cathode
  N1: Composant1.RESET, 2N2222.E
  N2: Composant1.5V, L7805CV.OUT, K3.COIL2, D4.cathode
  N3: Composant1.D28, 1K.Pin_0
  N4: Composant1.D44, IC1.In_1
  N5: Composant1.D45, IC1.In_2
  N6: Composant1.D46, IC1.In_3
  N7: Composant1.D47, R5.Pin_1
  N8: Composant1.D52, R6.Pin_1
  N9: 2N2222.B, 1K.Pin_1
  N10: L7805CV.GND, J1.PWR, IC1.COM_-_Common, K3.C1, K3.C2
  N11: IC1.Out_3, IC1.Out_2, LED1.green_cathode
  N12: IC1.Out_1, LED1.red_cathode
  N13: LED1.common_anode, K3.A
  N14: K3.COIL1, Q4.C, D4.anode
  N15: Q4.B, R5.Pin_0
  N16: R6.Pin_0, LED2.anode

notes:
  5V
  12V

// code stored in the sketch: Control Led RGB Arduino Ethernet.ino
#include "simtronyx_RGB_LED.h"
#include <Ethernet.h>
#include "decode_request.h"
#include "format_html.h"

IPAddress ip(192, 168, 1, 59);
byte mac[] = {
  0xDE, 0xAD, 0xBE, 0xEF, 0xFE, 0xED
};
int portWebserver = 8282;


#define REDPIN 46
#define GREENPIN 45 
#define BLUEPIN 44
int pinRelais=47; 
int pinReset=28;
int pinLed=52;

String status_led = "0";
simtronyx_RGB_LED strip(REDPIN,GREENPIN,BLUEPIN);

// overall brightness 
int brightness = 50;
// speed for animation / color transitions
int fadingDelay = 100;

#define FADING_STEPS 200
#define COLOR_HOLD 20


EthernetServer server(portWebserver);

void setup() {
  pinMode(pinRelais,OUTPUT); //pin en mode OUTPUT
  //digitalWrite(pinRelais,HIGH);
   // active la broche en sortie (OUTPUT)  
  pinMode(pinReset, OUTPUT);
  digitalWrite(pinReset, LOW);
  pinMode(pinLed, OUTPUT); 
  digitalWrite(pinLed, LOW);
  
  // Open serial communications and wait for port to open:
  Serial.begin(9600);
  
  while (!Serial) {
    ; // wait for serial port to connect. Needed for native USB port only
  }

  //init webserveur et connexion lan
  Serial.println("Connexion au réseaux en cours ...");
  // start the Ethernet connection and the server:
  Ethernet.begin(mac, ip);

  server.begin();
  Serial.print("server connecté!!  adresse :  ");
  Serial.print(Ethernet.localIP());
  Serial.print(" port : ");
  Serial.println(portWebserver);
  digitalWrite(pinLed, HIGH);
  strip.animateColorTypeSet(ANIMATETYPE_RGB);


}

void pushReset() 
{ 
   
  Serial.println("redemarage");
   delay(1000);
  // Déactive le reset forçant la sortie au niveau bas 
  digitalWrite(pinReset, HIGH);
  Serial.println("fin redemarage");
}

void loop() {
  strip.loop();
  
  EthernetClient client = server.available();
  if (client) {
    Serial.println("new client");
    // an http request ends with a blank line
    boolean currentLineIsBlank = true;
    while (client.connected()) {
      if (client.available()) {
        char c = client.read();
        Serial.write(c);


        String req = client.readStringUntil('\r');
        // Match the request
         if (req.indexOf("") != -10) {  //checks if you're on the main page

           String reponse_decodage = decode_request_http(req);
           Serial.println("");
           if(reponse_decodage == "reboot"){
            String repStatus = "HTTP/1.1 200 OK\r\n";
             repStatus += "Content-Type: text/html\r\n\r\n";
             repStatus += "<!DOCTYPE HTML>\r\n<html>\r\n";
             repStatus += "<body>\n";
             repStatus += "<span class='status_reboot'>";
             repStatus += "1";
             repStatus += "</span>\n";
             

            repStatus += "</body>\n";
            repStatus += "</html>\n";
          
            client.print(repStatus);
            
             delay(5000);
             pushReset() ;
             break;
           }
           if(reponse_decodage == "status"){

             String repStatus = "HTTP/1.1 200 OK\r\n";
             repStatus += "Content-Type: text/html\r\n\r\n";
             repStatus += "<!DOCTYPE HTML>\r\n<html>\r\n";
             repStatus += "<body>\n";
             repStatus += "<span class='status_led'>";
             repStatus += status_led;
             repStatus += "</span>\n";
             

            repStatus += "</body>\n";
            repStatus += "</html>\n";
            
           // client.print("status_led = ");
            //client.println("Status: 200");
            //client.println("Content-Type: text/html");
            client.print(repStatus);
            break;
           }
          
           else{
            String retour = action(reponse_decodage);
            /*
            if(retour == "1"){
                 String repStatus = "HTTP/1.1 200 OK\r\n";
                 repStatus += "Content-Type: text/html\r\n\r\n";
                 repStatus += "<!DOCTYPE HTML>\r\n<html>\r\n";
                 repStatus += "<body>\n";
                 repStatus += "<span class='status_led'>";
                 repStatus += retour;
                 repStatus += "</span>\n";
                 
    
                repStatus += "</body>\n";
                repStatus += "</html>\n";
                
               // client.print("status_led = ");
                //client.println("Status: 200");
                //client.println("Content-Type: text/html");
                client.print(repStatus);
                break;
              }
            if(retour == "0"){
                String repStatus = "HTTP/1.1 200 OK\r\n";
               repStatus += "Content-Type: text/html\r\n\r\n";
               repStatus += "<!DOCTYPE HTML>\r\n<html>\r\n";
               repStatus += "<body>\n";
               repStatus += "<span class='status_led'>";
               repStatus += 0;
               repStatus += "</span>\n";
               
  
              repStatus += "</body>\n";
              repStatus += "</html>\n";
              
             // client.print("status_led = ");
              //client.println("Status: 200");
              //client.println("Content-Type: text/html");
              client.print(repStatus);
              break;
              }
              */
           }
           
         }

         
        // if you've gotten to the end of the line (received a newline
        // character) and the line is blank, the http request has ended,
        // so you can send a reply
        if (c == '\n' && currentLineIsBlank) {
          // Prepare the response
          String s = format_page_web();
          
          client.println(s);
          break;
        }
        if (c == '\n') {
          // you're starting a new line
          currentLineIsBlank = true;
        } else if (c != '\r') {
          // you've gotten a character on the current line
          currentLineIsBlank = false;
        }
      }
    }
    // give the web browser time to receive the data
    delay(1);
    // close the connection:
    client.stop();
    Serial.println("client disconnected");
    
  }
  // strip.loop();
}


String action(String req){
  String retour = "0";
  if (req == "0xF740BF") { //checks if you clicked OFF
    status_led="0";
      strip.animateStop();
      digitalWrite(pinRelais,LOW); // off commande l'extinction
      delay(1000);
      Serial.println("OFF");
      retour = "1";
    }
    if (req == "0xF7C03F") { //checks if you clicked ON
      status_led="1";
      strip.animateStop();
      digitalWrite(pinRelais,HIGH); // on commande l'allumage
      delay(1000);
      Serial.println("ON");
      retour = "1";
    }
   /* if (req == "0xF720DF") { //red
      status_led="1";
      strip.animateStop();
      strip.setRGB(255,0,0);
      delay(1000);
      Serial.println("Rouge");
      retour = "1";
    }
*/
   
  if (req == "0xF700FF") { // brighter
    status_led="1";
      strip.useBrightnessAdjust( true );
      brightness = inc(brightness,10,100);
      strip.setBrightnessRGB(brightness);
      delay(1000);
      Serial.println(brightness);
      retour = "1";
    }

  if (req == "0xF7807F") { // darker
    status_led="1";
     strip.useBrightnessAdjust( true );
     brightness = dec(brightness,10);
      strip.setBrightnessRGB(brightness);
      delay(1000);
      Serial.println(brightness);
      retour = "1";
    }


  if (req == "0xF7D02F") { // slower
    status_led="1";
      fadingDelay = inc(fadingDelay,100,5000);
      strip.animateSpeedSet(fadingDelay);
      delay(1000);
      Serial.println("You clicked 9");
      retour = "1";
    }

  if (req == "0xF7F00F") { // faster
    status_led="1";
      fadingDelay = dec(fadingDelay, 100 );
      strip.animateSpeedSet(fadingDelay);
      delay(1000);
      Serial.println("You clicked 9");
      retour = "1";
    }

   if (req == "0xF7E817") { // fading Massage
    status_led="1";
      strip.animateStop();
      delay(50);
      digitalWrite(pinRelais,HIGH); // on commande l'allumage
      delay(50);
       strip.animateColorsClear();
       delay(50);
       strip.animateColorAdd(255,47,152,FADING_STEPS);
       delay(50);
       strip.animateColorAdd(175,0,90,FADING_STEPS);  
       delay(50);
       strip.animateColorAdd(145,14,178,FADING_STEPS);
       delay(50);
       strip.animateColorAdd(224,100,255,FADING_STEPS);
       delay(50);
       strip.animateColorAdd(211,36,255,FADING_STEPS);
       delay(50);
       strip.animateColorAdd(108,178,0,FADING_STEPS);
       delay(50);
       strip.animateColorAdd(178,255,62,FADING_STEPS);
       delay(50);
       strip.animateColorAdd(51,72,178,FADING_STEPS);
       delay(50);
       strip.animateColorAdd(98,124,255,FADING_STEPS);
       delay(50);
       strip.animateColorAdd(112,4,178,FADING_STEPS);
       delay(50);
       strip.animateStart();

      Serial.println("fading massage");
      retour = "1";
    }

    if (req == "0xD9ER18") { // fading Massage
      status_led="1";
      strip.animateStop();
      delay(50);
      digitalWrite(pinRelais,HIGH); // on commande l'allumage
      delay(50);
       strip.animateColorsClear();
       delay(50);
       strip.animateColorAdd(13,178,61,FADING_STEPS);
       delay(50);
       strip.animateColorAdd(62,255,178,FADING_STEPS); 
       delay(50); 
       strip.animateColorAdd(36,255,100,FADING_STEPS);
       delay(50);
       strip.animateColorAdd(178,1,0,FADING_STEPS);
       delay(50);
       strip.animateColorAdd(255,37,36,FADING_STEPS);
       delay(50);
       strip.animateColorAdd(178,13,136,FADING_STEPS);
       delay(50);
       strip.animateColorAdd(255,91,213,FADING_STEPS);
       delay(50);
       strip.animateColorAdd(255,36,199,FADING_STEPS);
       delay(50);
       strip.animateColorAdd(178,140,15,FADING_STEPS);
       delay(50);
       strip.animateColorAdd(36,65,255,FADING_STEPS);
       delay(50);
       strip.animateStart();
       Serial.println("fading relax");
       retour = "1";
    }

    if (req.indexOf("rgb:") != -1) { // add color to list RGB
        int startRgbRetour = req.indexOf("rgb:");
        String rgb = req.substring(startRgbRetour+4);
       
        if (getValue(rgb,'.',0) != -1 && getValue(rgb,'.',1) != -1 && getValue(rgb,'.',2) != -1 ) {
          String r = getValue(rgb,'.',0);
          String g = getValue(rgb,'.',1);
          String b = getValue(rgb,'.',2);

          int r_int = r.toInt();
          int g_int = g.toInt();
          int b_int = b.toInt();
          
  
          delay(100);
          strip.animateColorAdd(r_int,g_int,b_int,FADING_STEPS);
          retour = "1";
          Serial.print("Add Color : ");
          Serial.print(r_int);
          Serial.print(".");
          Serial.print(g_int);
          Serial.print(".");
          Serial.print(b_int);
          Serial.print(" To list Fading.");
          
        }
      }

      if (req.indexOf("color:") != -1) { // set Color
        
        int startRgbRetour = req.indexOf("color:");
        String rgb = req.substring(startRgbRetour+6);
      
        if (getValue(rgb,'.',0) != -1 && getValue(rgb,'.',1) != -1 && getValue(rgb,'.',2) != -1 ) {
          String r = getValue(rgb,'.',0);
          String g = getValue(rgb,'.',1);
          String b = getValue(rgb,'.',2);

          int r_int = r.toInt();
          int g_int = g.toInt();
          int b_int = b.toInt();
          
          digitalWrite(pinRelais,HIGH); // on commande l'allumage
          delay(100);
          status_led="1";
          strip.animateStop();
          delay(100);
          strip.setRGB(r_int,g_int,b_int);
          delay(1000);
         
          retour = "1";
          Serial.print("Set Color : ");
          Serial.print(r_int);
          Serial.print(".");
          Serial.print(g_int);
          Serial.print(".");
          Serial.println(b_int);
          
        }
      }
      if (req == "1xclear") { // Clear List Fadding
        
        
        strip.animateStop();
        delay(50); 
        strip.animateColorsClear();
        
        delay(1000);
        Serial.println("Clear LIst Fadding");
        retour = "1";
      }

      if (req == "1xstopfade") { // Stop Fadding
        status_led="0";
        digitalWrite(pinRelais,LOW); // off commande l'extinction
        delay(50);
        strip.animateStop();
        
        delay(1000);
        Serial.println("Stop Fadding");
        retour = "1";
      }

      if (req == "1xstartfade") { // Start Fadding
        status_led="0";
        digitalWrite(pinRelais,HIGH); // on commande l'allumage
        delay(50);
        strip.animateStart();
        
        delay(1000);
        Serial.println("Start Fadding");
        retour = "1";
      }

     
      
  return retour;
}


int inc( int in, int delta, int limit ) {
  int r = in + delta;
  if( r > limit ) r = limit;
  return r;
}

int dec( int in, int delta ) {
  int r = in - delta;
  if( r < 0 ) r = 0;
  return r;
}
